# Fritzing sketch SmartRoomController (saved by Fritzing 0.9.9b)
breadboards: 1

parts:
  S1 = Pushbutton [package="[THT]"]
  Teensy_3_2 = Teensy 3.1
  Water_Level_Sensor1 = Water Level Sensor
  R6 = Resistor [tolerance=±5% resistance=1k package="0805 [SMD]"]

nets:
  N1: S1.Pin_1, S1.Pin_2, R6.Pin_1
  3V3: S1.Pin_3, S1.Pin_4, Teensy_3_2.3V3, Water_Level_Sensor1.VCC
  GND: Teensy_3_2.GND, Water_Level_Sensor1.GND, R6.Pin_0

custom parts:
  Pushbutton: A generic pushbutton.
  Water Level Sensor: A water level sensor. This sensor operates at 3V to 5V. The Sig (signal) pin outputs an analogue signal that is in proportion to the amount of water in contact with the sensor.
